# Fritzing sketch module (saved by Fritzing 0.9.3b)
breadboards: 1

parts:
  MH-ET_LIVE_ESP32_DEVKIT1 = MH-ET LIVE ESP32 DEVKIT 38 pins
  Part1 = MQ-4
  Part2 = MQ-4
  Part3 = MQ-4
  Part4 = MQ-4
  Part5 = MicroSD Card Module

nets:
  N1: MH-ET_LIVE_ESP32_DEVKIT1.IO34, Part2.AO
  N2: MH-ET_LIVE_ESP32_DEVKIT1.IO35, Part1.AO
  N3: MH-ET_LIVE_ESP32_DEVKIT1.IO32, Part3.AO
  N4: MH-ET_LIVE_ESP32_DEVKIT1.IO33, Part4.AO
  N5: MH-ET_LIVE_ESP32_DEVKIT1.IO26, Part5.CS
  GND: MH-ET_LIVE_ESP32_DEVKIT1.CMD, Part1.GND, Part2.GND, Part3.GND, Part4.GND, Part5.GND
  VCC: MH-ET_LIVE_ESP32_DEVKIT1.5V, Part1.VCC, Part2.VCC, Part3.VCC, Part4.VCC, Part5.VCC
  N6: MH-ET_LIVE_ESP32_DEVKIT1.IO23, Part5.MOSI
  N7: MH-ET_LIVE_ESP32_DEVKIT1.IO19, Part5.MISO
  N8: MH-ET_LIVE_ESP32_DEVKIT1.IO18, Part5.SCK

notes:
  The above MQs are MQ-5s. The Q-5 fritzing part was not found online
  First MQ-5
  Second MQ-5
  First MQ-4
  Second MQ-4

custom parts:
  MH-ET LIVE ESP32 DEVKIT 38 pins: http://mh.nodebb.com/topic/2/mh-et-live-esp32-devkit
